// Logisim project decoder.circ as structural Verilog
module decoder (
  input  in_1,
  input  in_2,
  output out_3,
  output out_4,
  output out_5,
  output out_6
);

  wire nand_1_out, nand_2_out, nand_3_out, nand_4_out, nand_5_out, nand_6_out, nand_7_out, nand_8_out,
       nand_9_out, nand_10_out, nand_11_out, nand_12_out;

  nand nand_1 (nand_1_out, in_1, in_1);
  nand nand_2 (nand_2_out, in_2, in_2);
  nand nand_3 (nand_3_out, in_1, in_1);
  nand nand_4 (nand_4_out, in_2, in_2);
  nand nand_5 (nand_5_out, in_2, in_2, in_2);
  nand nand_6 (nand_6_out, in_1, in_1);
  nand nand_7 (nand_7_out, in_1, in_2);
  nand nand_8 (nand_8_out, in_1, in_2);
  nand nand_9 (nand_9_out, nand_1_out, nand_2_out);
  nand nand_10 (nand_10_out, nand_3_out, nand_4_out);
  nand nand_11 (nand_11_out, in_1, nand_5_out);
  nand nand_12 (nand_12_out, nand_6_out, in_2);
  nand nand_13 (out_6, nand_7_out, nand_8_out);
  nand nand_14 (out_3, nand_9_out, nand_10_out);
  nand nand_15 (out_4, nand_11_out, nand_11_out);
  nand nand_16 (out_5, nand_12_out, nand_12_out);
endmodule

module multiBit_MUX (
  input  [3:0] in_1,
  input  [3:0] in_2,
  input  [3:0] in_3,
  input  [3:0] in_4
);

  Multiplexer #(.select(2)) multiplexer_1 ();  // open: in0, in1, in2, in3, out, sel, en
  Multiplexer #(.select(2)) multiplexer_2 ();  // open: in0, in1, in2, in3, out, sel, en
  Multiplexer #(.select(2)) multiplexer_3 ();  // open: in0, in1, in2, in3, out, sel, en
  Multiplexer #(.select(2)) multiplexer_4 ();  // open: in0, in1, in2, in3, out, sel, en
  // Pins of 1 and 4 bits meet at in_2
endmodule
